// Logisim project Logisim Design.circ as structural Verilog
module ALU (
  input  [15:0] Input,
  input  [15:0] Input_2,
  input  [1:0] ALU_Control_Signal,
  output Zero_Signal__for_branching,
  output [15:0] Output
);

  wire [15:0] adder_1_out, and_1_out, or_1_out, subtractor_1_out;

  Adder #(.width(16)) adder_1 (.a(Input), .b(Input_2), .out(adder_1_out));  // open: cin, cout
  Subtractor #(.width(16)) subtractor_1 (.a(Input), .b(Input_2), .out(subtractor_1_out));  // open: bin, bout
  assign and_1_out = Input & Input_2;  // AND_Gate and_1, 16 bits wide
  assign or_1_out = Input | Input_2;  // OR_Gate or_1, 16 bits wide
  Multiplexer #(.select(2), .width(16), .enable("false")) multiplexer_1 (
    .in0(adder_1_out), .in1(subtractor_1_out), .in2(and_1_out), .in3(or_1_out), .out(Output),
    .sel(ALU_Control_Signal));
  nor nor_1 (Zero_Signal__for_branching, Output[15], Output[14], Output[13], Output[12], Output[11], Output[10], Output[9], Output[8], Output[7], Output[6], Output[5], Output[4], Output[3], Output[2], Output[1], Output[0]);
endmodule

module Main_Control (
  input  [1:0] Operation_Code,
  output out_2,
  output out_3,
  output out_4,
  output out_5,
  output Memoty_Write,
  output out_7,
  output out_8,
  output Memory_Read,
  output out_10,
  output out_11
);

  wire not_1_out, not_2_out, not_3_out, not_4_out;

  not not_1 (not_1_out, Operation_Code[0]);
  not not_2 (not_2_out, Operation_Code[1]);
  not not_3 (not_3_out, Operation_Code[1]);
  not not_4 (not_4_out, Operation_Code[0]);
  and R_Formats (out_4, not_1_out, not_2_out);
  and Load__lw (Memory_Read, Operation_Code[0], not_3_out);
  and Store__sw (Memoty_Write, not_4_out, Operation_Code[1]);
  and beq (out_7, Operation_Code[0], Operation_Code[1]);
  or Register_Write (out_2, out_4, Memory_Read);
  or ALU_Source (out_3, Memory_Read, Memoty_Write);
  or Extension_Operation (out_8, Memory_Read, Memoty_Write, out_7);

  assign out_5 = Memory_Read;
  assign out_10 = out_4;
  assign out_11 = out_7;

  // Notes on the sheet:
  //   Register Destination
  //   Memory to Register
  //   Branch
  //   ALUopt<1>
  //   ALUopt<0>
endmodule

module ALU_Control (
  input  [4:0] Function_Code,
  input  [1:0] ALUopt,
  output [1:0] ALU_Control_Signal
);

  Multiplexer #(.width(2), .enable("false")) multiplexer_1 (
    .in0(ALUopt), .in1(Function_Code[1:0]), .out(ALU_Control_Signal), .sel(ALUopt[1]));
endmodule

module Registe_File (
  input  [2:0] Read_Register_1,
  input  [2:0] Read_Register_2,
  input  [2:0] Write_Register,
  input  Registe_Write,
  input  [15:0] Write_Data,
  output [15:0] Read_Data_1,
  output [15:0] Read_Data_2
);

  wire and_1_out, and_2_out, and_3_out, and_4_out, and_5_out, and_6_out, and_7_out, and_8_out, Clock_out,
       decoder_1_out0, decoder_1_out1, decoder_1_out2, decoder_1_out3, decoder_1_out4, decoder_1_out5,
       decoder_1_out6, decoder_1_out7;
  wire [15:0] register_1_q, register_2_q, register_3_q, register_4_q, register_5_q, register_6_q,
       register_7_q, register_8_q;

  Decoder #(.select(3)) decoder_1 (
    .out0(decoder_1_out0), .out1(decoder_1_out1), .out2(decoder_1_out2), .out3(decoder_1_out3),
    .out4(decoder_1_out4), .out5(decoder_1_out5), .out6(decoder_1_out6), .out7(decoder_1_out7),
    .sel(Write_Register));  // open: en
  and and_1 (and_1_out, decoder_1_out0, Registe_Write);
  and and_2 (and_2_out, decoder_1_out1, Registe_Write);
  and and_3 (and_3_out, decoder_1_out2, Registe_Write);
  and and_4 (and_4_out, decoder_1_out3, Registe_Write);
  and and_5 (and_5_out, decoder_1_out4, Registe_Write);
  and and_6 (and_6_out, decoder_1_out5, Registe_Write);
  and and_7 (and_7_out, decoder_1_out6, Registe_Write);
  and and_8 (and_8_out, decoder_1_out7, Registe_Write);
  Clock Clock (.out(Clock_out));
  Register #(.width(16)) register_1 (.D(Write_Data), .Q(register_1_q), .clk(Clock_out), .clr(and_1_out));  // open: en
  Register #(.width(16)) register_2 (.D(Write_Data), .Q(register_2_q), .clk(Clock_out), .clr(and_2_out));  // open: en
  Register #(.width(16)) register_3 (.D(Write_Data), .Q(register_3_q), .clk(Clock_out), .clr(and_3_out));  // open: en
  Register #(.width(16)) register_4 (.D(Write_Data), .Q(register_4_q), .clk(Clock_out), .clr(and_4_out));  // open: en
  Register #(.width(16)) register_5 (.D(Write_Data), .Q(register_5_q), .clk(Clock_out), .clr(and_5_out));  // open: en
  Register #(.width(16)) register_6 (.D(Write_Data), .Q(register_6_q), .clk(Clock_out), .clr(and_6_out));  // open: en
  Register #(.width(16)) register_7 (.D(Write_Data), .Q(register_7_q), .clk(Clock_out), .clr(and_7_out));  // open: en
  Register #(.width(16)) register_8 (.D(Write_Data), .Q(register_8_q), .clk(Clock_out), .clr(and_8_out));  // open: en
  Multiplexer #(.select(3), .width(16)) multiplexer_1 (
    .in0(register_1_q), .in1(register_2_q), .in2(register_3_q), .in3(register_4_q), .in4(register_5_q),
    .in5(register_6_q), .in6(register_7_q), .in7(register_8_q), .out(Read_Data_1), .sel(Read_Register_1));  // open: en
  Multiplexer #(.select(3), .width(16)) multiplexer_2 (
    .in0(register_1_q), .in1(register_2_q), .in2(register_3_q), .in3(register_4_q), .in4(register_5_q),
    .in5(register_6_q), .in6(register_7_q), .in7(register_8_q), .out(Read_Data_2), .sel(Read_Register_2));  // open: en
endmodule
